// Logisim project 1mux.circ as structural Verilog
module _2_1_mux (
  input  in_0,
  input  in_01,
  input  select,
  output out
);

  wire and_1_out, and_2_out, not_1_out;

  not not_1 (not_1_out, select);
  and and_1 (and_1_out, in_0, not_1_out);
  and and_2 (and_2_out, in_01, select);
  or or_1 (out, and_1_out, and_2_out);
endmodule

module _4_1_mux (
  input  in_00,
  input  in_01,
  input  in_10,
  input  in_11,
  input  [1:0] slelect,
  output out
);

  wire n2_1_mux_1_out, n2_1_mux_2_out;

  _2_1_mux u_2_1_mux_1 (.in_0(in_00), .in_01(in_01), .select(slelect[0]), .out(n2_1_mux_1_out));
  _2_1_mux u_2_1_mux_2 (.in_0(in_10), .in_01(in_11), .select(slelect[0]), .out(n2_1_mux_2_out));
  _2_1_mux u_2_1_mux_3 (.in_0(n2_1_mux_1_out), .in_01(n2_1_mux_2_out), .select(slelect[1]), .out(out));
endmodule
