// Logisim project 8bitShifitCircle.circ as structural Verilog: 2 circuits, main circuit shift
module shift (
  input  s0,
  input  s1,
  input  s2,
  input  d0,
  input  d1,
  input  d2,
  input  d3,
  input  d4,
  input  d5,
  input  d6,
  input  d7,
  output q0,
  output q1,
  output q2,
  output q3,
  output q4,
  output q5,
  output q6,
  output q7
);

  wire and_1_out, and_2_out, and_3_out, and_4_out, and_5_out, and_6_out, and_7_out, and_8_out, and_9_out,
       and_10_out, and_11_out, and_12_out, and_13_out, and_14_out, and_15_out, and_16_out, and_17_out,
       and_18_out, and_19_out, and_20_out, and_21_out, and_22_out, and_23_out, and_24_out, and_25_out,
       and_26_out, and_27_out, and_28_out, and_29_out, and_30_out, and_31_out, and_32_out, and_33_out,
       and_34_out, and_35_out, and_36_out, and_37_out, and_38_out, and_39_out, and_40_out, and_41_out,
       and_42_out, and_43_out, and_44_out, and_45_out, and_46_out, and_47_out, and_48_out, and_49_out,
       and_50_out, and_51_out, and_52_out, and_53_out, and_54_out, and_55_out, and_56_out, and_57_out,
       and_58_out, and_59_out, and_60_out, and_61_out, and_62_out, and_63_out, and_64_out, not_1_out,
       not_2_out, not_3_out, not_4_out, not_5_out, not_6_out, not_7_out, not_8_out, not_9_out, not_10_out,
       not_11_out, not_12_out, not_13_out, not_14_out, not_15_out, not_16_out, not_17_out, not_18_out,
       not_19_out, not_20_out, not_21_out, not_22_out, not_23_out, not_24_out, not_25_out, not_26_out,
       not_27_out, not_28_out, not_29_out, not_30_out, not_31_out, not_32_out, not_33_out, not_34_out,
       not_35_out, not_36_out, not_37_out, not_38_out, not_39_out, not_40_out, not_41_out, not_42_out,
       not_43_out, not_44_out, not_45_out, not_46_out, not_47_out, not_48_out, not_49_out, not_50_out,
       not_51_out, not_52_out, not_53_out, not_54_out, not_55_out, not_56_out, not_57_out, not_58_out,
       not_59_out, not_60_out, not_61_out, not_62_out, not_63_out, not_64_out, not_65_out, not_66_out,
       not_67_out, not_68_out, not_69_out, not_70_out, not_71_out, not_72_out, not_73_out, not_74_out,
       not_75_out, not_76_out, not_77_out, not_78_out, not_79_out, not_80_out, not_81_out, not_82_out,
       not_83_out, not_84_out, not_85_out, not_86_out, not_87_out, not_88_out, not_89_out, not_90_out,
       not_91_out, not_92_out, not_93_out, not_94_out, not_95_out, not_96_out;

  not not_1 (not_1_out, s0);
  not not_2 (not_2_out, s1);
  not not_3 (not_3_out, s2);
  not not_4 (not_4_out, s1);
  not not_5 (not_5_out, s2);
  not not_6 (not_6_out, s0);
  not not_7 (not_7_out, s2);
  not not_8 (not_8_out, s2);
  not not_9 (not_9_out, s0);
  not not_10 (not_10_out, s1);
  not not_11 (not_11_out, s1);
  not not_12 (not_12_out, s0);
  not not_13 (not_13_out, s0);
  not not_14 (not_14_out, s1);
  not not_15 (not_15_out, s2);
  not not_16 (not_16_out, s1);
  not not_17 (not_17_out, s2);
  not not_18 (not_18_out, s0);
  not not_19 (not_19_out, s2);
  not not_20 (not_20_out, s2);
  not not_21 (not_21_out, s0);
  not not_22 (not_22_out, s1);
  not not_23 (not_23_out, s1);
  not not_24 (not_24_out, s0);
  not not_25 (not_25_out, s0);
  not not_26 (not_26_out, s1);
  not not_27 (not_27_out, s2);
  not not_28 (not_28_out, s1);
  not not_29 (not_29_out, s2);
  not not_30 (not_30_out, s0);
  not not_31 (not_31_out, s2);
  not not_32 (not_32_out, s2);
  not not_33 (not_33_out, s0);
  not not_34 (not_34_out, s1);
  not not_35 (not_35_out, s1);
  not not_36 (not_36_out, s0);
  not not_37 (not_37_out, s0);
  not not_38 (not_38_out, s1);
  not not_39 (not_39_out, s2);
  not not_40 (not_40_out, s1);
  not not_41 (not_41_out, s2);
  not not_42 (not_42_out, s0);
  not not_43 (not_43_out, s2);
  not not_44 (not_44_out, s2);
  not not_45 (not_45_out, s0);
  not not_46 (not_46_out, s1);
  not not_47 (not_47_out, s1);
  not not_48 (not_48_out, s0);
  not not_49 (not_49_out, s0);
  not not_50 (not_50_out, s1);
  not not_51 (not_51_out, s2);
  not not_52 (not_52_out, s1);
  not not_53 (not_53_out, s2);
  not not_54 (not_54_out, s0);
  not not_55 (not_55_out, s2);
  not not_56 (not_56_out, s2);
  not not_57 (not_57_out, s0);
  not not_58 (not_58_out, s1);
  not not_59 (not_59_out, s1);
  not not_60 (not_60_out, s0);
  not not_61 (not_61_out, s0);
  not not_62 (not_62_out, s1);
  not not_63 (not_63_out, s2);
  not not_64 (not_64_out, s1);
  not not_65 (not_65_out, s2);
  not not_66 (not_66_out, s0);
  not not_67 (not_67_out, s2);
  not not_68 (not_68_out, s2);
  not not_69 (not_69_out, s0);
  not not_70 (not_70_out, s1);
  not not_71 (not_71_out, s1);
  not not_72 (not_72_out, s0);
  not not_73 (not_73_out, s0);
  not not_74 (not_74_out, s1);
  not not_75 (not_75_out, s2);
  not not_76 (not_76_out, s1);
  not not_77 (not_77_out, s2);
  not not_78 (not_78_out, s0);
  not not_79 (not_79_out, s2);
  not not_80 (not_80_out, s2);
  not not_81 (not_81_out, s0);
  not not_82 (not_82_out, s1);
  not not_83 (not_83_out, s1);
  not not_84 (not_84_out, s0);
  not not_85 (not_85_out, s0);
  not not_86 (not_86_out, s1);
  not not_87 (not_87_out, s2);
  not not_88 (not_88_out, s1);
  not not_89 (not_89_out, s2);
  not not_90 (not_90_out, s0);
  not not_91 (not_91_out, s2);
  not not_92 (not_92_out, s2);
  not not_93 (not_93_out, s0);
  not not_94 (not_94_out, s1);
  not not_95 (not_95_out, s1);
  not not_96 (not_96_out, s0);
  and and_1 (and_1_out, not_1_out, not_2_out, not_3_out, d0);
  and and_2 (and_2_out, s0, not_4_out, not_5_out, d7);
  and and_3 (and_3_out, not_6_out, s1, not_7_out, d6);
  and and_4 (and_4_out, s0, s1, not_8_out, d5);
  and and_5 (and_5_out, not_9_out, not_10_out, s2, d4);
  and and_6 (and_6_out, s0, not_11_out, s2, d3);
  and and_7 (and_7_out, not_12_out, s1, s2, d2);
  and and_8 (and_8_out, s0, s1, s2, d1);
  and and_9 (and_9_out, not_13_out, not_14_out, not_15_out, d1);
  and and_10 (and_10_out, s0, not_16_out, not_17_out, d0);
  and and_11 (and_11_out, not_18_out, s1, not_19_out, d7);
  and and_12 (and_12_out, s0, s1, not_20_out, d6);
  and and_13 (and_13_out, not_21_out, not_22_out, s2, d5);
  and and_14 (and_14_out, s0, not_23_out, s2, d4);
  and and_15 (and_15_out, not_24_out, s1, s2, d3);
  and and_16 (and_16_out, s0, s1, s2, d2);
  and and_17 (and_17_out, not_25_out, not_26_out, not_27_out, d2);
  and and_18 (and_18_out, s0, not_28_out, not_29_out, d1);
  and and_19 (and_19_out, not_30_out, s1, not_31_out, d0);
  and and_20 (and_20_out, s0, s1, not_32_out, d7);
  and and_21 (and_21_out, not_33_out, not_34_out, s2, d6);
  and and_22 (and_22_out, s0, not_35_out, s2, d5);
  and and_23 (and_23_out, not_36_out, s1, s2, d4);
  and and_24 (and_24_out, s0, s1, s2, d3);
  and and_25 (and_25_out, not_37_out, not_38_out, not_39_out, d3);
  and and_26 (and_26_out, s0, not_40_out, not_41_out, d2);
  and and_27 (and_27_out, not_42_out, s1, not_43_out, d1);
  and and_28 (and_28_out, s0, s1, not_44_out, d0);
  and and_29 (and_29_out, not_45_out, not_46_out, s2, d7);
  and and_30 (and_30_out, s0, not_47_out, s2, d6);
  and and_31 (and_31_out, not_48_out, s1, s2, d5);
  and and_32 (and_32_out, s0, s1, s2, d4);
  and and_33 (and_33_out, not_49_out, not_50_out, not_51_out, d4);
  and and_34 (and_34_out, s0, not_52_out, not_53_out, d3);
  and and_35 (and_35_out, not_54_out, s1, not_55_out, d2);
  and and_36 (and_36_out, s0, s1, not_56_out, d1);
  and and_37 (and_37_out, not_57_out, not_58_out, s2, d0);
  and and_38 (and_38_out, s0, not_59_out, s2, d7);
  and and_39 (and_39_out, not_60_out, s1, s2, d6);
  and and_40 (and_40_out, s0, s1, s2, d5);
  and and_41 (and_41_out, not_61_out, not_62_out, not_63_out, d5);
  and and_42 (and_42_out, s0, not_64_out, not_65_out, d4);
  and and_43 (and_43_out, not_66_out, s1, not_67_out, d3);
  and and_44 (and_44_out, s0, s1, not_68_out, d2);
  and and_45 (and_45_out, not_69_out, not_70_out, s2, d1);
  and and_46 (and_46_out, s0, not_71_out, s2, d0);
  and and_47 (and_47_out, not_72_out, s1, s2, d7);
  and and_48 (and_48_out, s0, s1, s2, d6);
  and and_49 (and_49_out, not_73_out, not_74_out, not_75_out, d6);
  and and_50 (and_50_out, s0, not_76_out, not_77_out, d5);
  and and_51 (and_51_out, not_78_out, s1, not_79_out, d4);
  and and_52 (and_52_out, s0, s1, not_80_out, d3);
  and and_53 (and_53_out, not_81_out, not_82_out, s2, d2);
  and and_54 (and_54_out, s0, not_83_out, s2, d1);
  and and_55 (and_55_out, not_84_out, s1, s2, d0);
  and and_56 (and_56_out, s0, s1, s2, d7);
  and and_57 (and_57_out, not_85_out, not_86_out, not_87_out, d7);
  and and_58 (and_58_out, s0, not_88_out, not_89_out, d6);
  and and_59 (and_59_out, not_90_out, s1, not_91_out, d5);
  and and_60 (and_60_out, s0, s1, not_92_out, d4);
  and and_61 (and_61_out, not_93_out, not_94_out, s2, d3);
  and and_62 (and_62_out, s0, not_95_out, s2, d2);
  and and_63 (and_63_out, not_96_out, s1, s2, d1);
  and and_64 (and_64_out, s0, s1, s2, d0);
  or or_1 (q0, and_1_out, and_2_out, and_3_out, and_4_out, and_5_out, and_6_out, and_7_out, and_8_out);
  or or_2 (q1, and_9_out, and_10_out, and_11_out, and_12_out, and_13_out, and_14_out, and_15_out, and_16_out);
  or or_3 (q2, and_17_out, and_18_out, and_19_out, and_20_out, and_21_out, and_22_out, and_23_out, and_24_out);
  or or_4 (q3, and_25_out, and_26_out, and_27_out, and_28_out, and_29_out, and_30_out, and_31_out, and_32_out);
  or or_5 (q4, and_33_out, and_34_out, and_35_out, and_36_out, and_37_out, and_38_out, and_39_out, and_40_out);
  or or_6 (q5, and_41_out, and_42_out, and_43_out, and_44_out, and_45_out, and_46_out, and_47_out, and_48_out);
  or or_7 (q6, and_49_out, and_50_out, and_51_out, and_52_out, and_53_out, and_54_out, and_55_out, and_56_out);
  or or_8 (q7, and_57_out, and_58_out, and_59_out, and_60_out, and_61_out, and_62_out, and_63_out, and_64_out);
endmodule

module main (
  input  [2:0] in_1,
  input  [7:0] in_2,
  output [7:0] out_3
);

  shift shift_1 (
    .s0(in_1[0]), .s1(in_1[1]), .s2(in_1[2]), .d0(in_2[0]), .d1(in_2[1]), .d2(in_2[2]), .d3(in_2[3]),
    .d4(in_2[4]), .d5(in_2[5]), .d6(in_2[6]), .d7(in_2[7]), .q0(out_3[0]), .q1(out_3[1]), .q2(out_3[2]),
    .q3(out_3[3]), .q4(out_3[4]), .q5(out_3[5]), .q6(out_3[6]), .q7(out_3[7]));
endmodule
