// Logisim project 8lights.circ as structural Verilog: 2 circuits, main circuit main
module main (
  input  in_1,
  input  in_2
);

  wire clock_1_out, clock_2_out, decoder_1_out0, decoder_1_out1, decoder_1_out2, decoder_1_out3,
       decoder_1_out4, decoder_1_out5, decoder_1_out6, decoder_1_out7, n8mux_1_out_18, n8mux_1_out_19,
       n8mux_1_out_20, n8mux_1_out_21, n8mux_1_out_22, n8mux_1_out_23, n8mux_1_out_24, n8mux_1_out_25,
       not_1_out, not_2_out, or_1_out, or_2_out, register_1_q;
  wire [2:0] adder_1_out, register_2_q;
  wire [3:0] demultiplexer_1_out0, demultiplexer_1_out1;

  not not_1 (not_1_out, register_1_q);
  Register #(.width(1)) register_1 (.D(not_1_out), .Q(register_1_q), .clk(clock_1_out), .clr(or_1_out));  // open: en
  Clock clock_1 (.out(clock_1_out));
  not not_2 (not_2_out, in_1);
  or or_1 (or_1_out, not_2_out, in_2);
  Demultiplexer #(.width(4)) demultiplexer_1 (
    .out0(demultiplexer_1_out0), .out1(demultiplexer_1_out1), .in(4'b1111), .sel(register_1_q));  // open: en
  Adder #(.width(3)) adder_1 (.a(3'b001), .b(register_2_q), .out(adder_1_out));  // open: cin, cout
  Register #(.width(3)) register_2 (.D(adder_1_out), .Q(register_2_q), .clk(clock_2_out), .clr(or_2_out));  // open: en
  Clock clock_2 (.out(clock_2_out));
  Decoder #(.select(3)) decoder_1 (
    .out0(decoder_1_out0), .out1(decoder_1_out1), .out2(decoder_1_out2), .out3(decoder_1_out3),
    .out4(decoder_1_out4), .out5(decoder_1_out5), .out6(decoder_1_out6), .out7(decoder_1_out7),
    .sel(register_2_q));  // open: en
  or or_2 (or_2_out, in_2, in_1);
  _8mux u_8mux_1 (
    .in_1(decoder_1_out0), .in_2(decoder_1_out1), .in_3(decoder_1_out2), .in_4(decoder_1_out3),
    .in_5(decoder_1_out4), .in_6(decoder_1_out5), .in_7(decoder_1_out6), .in_8(decoder_1_out7),
    .in_9(demultiplexer_1_out0[0]), .in_10(demultiplexer_1_out0[1]), .in_11(demultiplexer_1_out0[2]),
    .in_12(demultiplexer_1_out0[3]), .in_13(demultiplexer_1_out1[0]), .in_14(demultiplexer_1_out1[1]),
    .in_15(demultiplexer_1_out1[2]), .in_16(demultiplexer_1_out1[3]), .in_17(in_1), .out_18(n8mux_1_out_18),
    .out_19(n8mux_1_out_19), .out_20(n8mux_1_out_20), .out_21(n8mux_1_out_21), .out_22(n8mux_1_out_22),
    .out_23(n8mux_1_out_23), .out_24(n8mux_1_out_24), .out_25(n8mux_1_out_25));
  LED led_1 (.in(n8mux_1_out_18));
  LED led_2 (.in(n8mux_1_out_19));
  LED led_3 (.in(n8mux_1_out_20));
  LED led_4 (.in(n8mux_1_out_21));
  LED led_5 (.in(n8mux_1_out_22));
  LED led_6 (.in(n8mux_1_out_23));
  LED led_7 (.in(n8mux_1_out_24));
  LED led_8 (.in(n8mux_1_out_25));
endmodule

module _8mux (
  input  in_1,
  input  in_2,
  input  in_3,
  input  in_4,
  input  in_5,
  input  in_6,
  input  in_7,
  input  in_8,
  input  in_9,
  input  in_10,
  input  in_11,
  input  in_12,
  input  in_13,
  input  in_14,
  input  in_15,
  input  in_16,
  input  in_17,
  output out_18,
  output out_19,
  output out_20,
  output out_21,
  output out_22,
  output out_23,
  output out_24,
  output out_25
);

  Multiplexer #(.enable("false")) multiplexer_1 (.in0(in_1), .in1(in_9), .out(out_18), .sel(in_17));
  Multiplexer #(.enable("false")) multiplexer_2 (.in0(in_2), .in1(in_10), .out(out_19), .sel(in_17));
  Multiplexer #(.enable("false")) multiplexer_3 (.in0(in_3), .in1(in_11), .out(out_20), .sel(in_17));
  Multiplexer #(.enable("false")) multiplexer_4 (.in0(in_4), .in1(in_12), .out(out_21), .sel(in_17));
  Multiplexer #(.enable("false")) multiplexer_5 (.in0(in_5), .in1(in_13), .out(out_22), .sel(in_17));
  Multiplexer #(.enable("false")) multiplexer_6 (.in0(in_6), .in1(in_14), .out(out_23), .sel(in_17));
  Multiplexer #(.enable("false")) multiplexer_7 (.in0(in_7), .in1(in_15), .out(out_24), .sel(in_17));
  Multiplexer #(.enable("false")) multiplexer_8 (.in0(in_8), .in1(in_16), .out(out_25), .sel(in_17));
endmodule
