// Logisim project D&P.circ as structural Verilog: 2 circuits, main circuit main
module main (
  input  [3:0] in_1,
  output D,
  output P
);

  D_P d_p_1 (.a0(in_1[0]), .a1(in_1[1]), .a2(in_1[2]), .a3(in_1[3]), .D(D), .P(P));
endmodule

module D_P (
  input  a0,
  input  a1,
  input  a2,
  input  a3,
  output D,
  output P
);

  wire and_1_out, and_2_out, and_3_out, and_4_out, and_5_out, and_6_out, and_7_out, and_8_out, and_9_out,
       and_10_out, not_1_out, not_2_out, not_3_out, not_4_out, not_5_out, not_6_out, not_7_out, not_8_out,
       not_9_out, not_10_out, not_11_out, not_12_out, not_13_out, not_14_out, not_15_out, not_16_out,
       not_17_out;

  not not_1 (not_1_out, a3);
  not not_2 (not_2_out, a2);
  not not_3 (not_3_out, a1);
  not not_4 (not_4_out, a0);
  not not_5 (not_5_out, a3);
  not not_6 (not_6_out, a2);
  not not_7 (not_7_out, a3);
  not not_8 (not_8_out, a0);
  not not_9 (not_9_out, a2);
  not not_10 (not_10_out, a1);
  not not_11 (not_11_out, a1);
  not not_12 (not_12_out, a0);
  not not_13 (not_13_out, a2);
  and and_1 (and_1_out, a1, not_13_out, not_14_out);
  not not_14 (not_14_out, a3);
  and and_2 (and_2_out, a0, not_15_out, a2);
  not not_15 (not_15_out, a1);
  and and_3 (and_3_out, a0, a1, not_16_out);
  not not_16 (not_16_out, a2);
  and and_4 (and_4_out, a0, a1, not_17_out);
  not not_17 (not_17_out, a3);
  and and_5 (and_5_out, not_1_out, not_2_out, not_3_out, not_4_out);
  and and_6 (and_6_out, not_5_out, not_6_out, a1, a0);
  and and_7 (and_7_out, not_7_out, a2, a1, not_8_out);
  and and_8 (and_8_out, a3, not_9_out, not_10_out, a0);
  and and_9 (and_9_out, a3, a2, not_11_out, not_12_out);
  and and_10 (and_10_out, a3, a2, a1, a0);
  or or_1 (P, and_1_out, and_2_out, and_3_out, and_4_out);
  or or_2 (D, and_5_out, and_6_out, and_7_out, and_8_out, and_9_out, and_10_out);
endmodule
