// Logisim project P0CRC.circ as structural Verilog: 2 circuits, main circuit CRC
module CRC (
  input  [7:0] in_1,
  input  [3:0] in_2,
  output [10:0] out_3
);

  wire [2:0] _1sto, _2ndo, _3rdo, _4tho, _5tho, _6tho, _7tho;

  _4bit_mod2div u_4bit_mod2div_1 (.bedived({_6tho, 1'b0}), .diver(in_2), .remainder(_7tho));
  _4bit_mod2div u_4bit_mod2div_2 (.bedived({_7tho, 1'b0}), .diver(in_2), .remainder(out_3[2:0]));
  _4bit_mod2div u_4bit_mod2div_3 (.bedived(in_1[7:4]), .diver(in_2), .remainder(_1sto));
  _4bit_mod2div u_4bit_mod2div_4 (.bedived({_1sto, in_1[3]}), .diver(in_2), .remainder(_2ndo));
  _4bit_mod2div u_4bit_mod2div_5 (.bedived({_2ndo, in_1[2]}), .diver(in_2), .remainder(_3rdo));
  _4bit_mod2div u_4bit_mod2div_6 (.bedived({_3rdo, in_1[1]}), .diver(in_2), .remainder(_4tho));
  _4bit_mod2div u_4bit_mod2div_7 (.bedived({_4tho, in_1[0]}), .diver(in_2), .remainder(_5tho));
  _4bit_mod2div u_4bit_mod2div_8 (.bedived({_5tho, 1'b0}), .diver(in_2), .remainder(_6tho));

  assign out_3[10:3] = in_1;

  // Other names for the same wires on the sheet: diver[3:0] = in_2; _8tho[2:0] = out_3[2:0]; _5thi = in_1[0];
  //   orig[7:0] = in_1; _4thi = in_1[1]; _3rdi = in_1[2]; _2ndi = in_1[3]; _1sti[3:0] = in_1[7:4]
endmodule

module _4bit_mod2div (
  input  [3:0] bedived,
  input  [3:0] diver,
  output [2:0] remainder
);

  wire [3:0] xor_1_out;

  assign xor_1_out = bedived ^ diver;  // XOR_Gate xor_1, 4 bits wide
  Multiplexer #(.width(3), .enable("false")) multiplexer_1 (
    .in0(bedived[2:0]), .in1(xor_1_out[2:0]), .out(remainder), .sel(bedived[3]));
endmodule
