// Logisim project P0Q1Guess.circ as structural Verilog: 4 circuits, main circuit 4bitadder
module _4bitadder (
  input  [3:0] in_1,
  input  [3:0] in_2,
  output [3:0] _4bitsum,
  output \output 
);

  wire n1bitadder_1_flag, n1bitadder_2_flag, n1bitadder_3_flag;

  _1bitadder u_1bitadder_1 (
    .add1(in_1[0]), .add2(in_2[0]), .preflag(1'b0), .sum(_4bitsum[0]), .flag(n1bitadder_1_flag));
  _1bitadder u_1bitadder_2 (
    .add1(in_1[1]), .add2(in_2[1]), .preflag(n1bitadder_1_flag), .sum(_4bitsum[1]), .flag(n1bitadder_2_flag));
  _1bitadder u_1bitadder_3 (
    .add1(in_1[2]), .add2(in_2[2]), .preflag(n1bitadder_2_flag), .sum(_4bitsum[2]), .flag(n1bitadder_3_flag));
  _1bitadder u_1bitadder_4 (
    .add1(in_1[3]), .add2(in_2[3]), .preflag(n1bitadder_3_flag), .sum(_4bitsum[3]), .flag(\output ));
endmodule

module _1bitadder (
  input  add1,
  input  add2,
  input  preflag,
  output sum,
  output flag
);

  wire and_1_out, and_2_out, and_3_out, and_4_out, and_5_out, and_6_out, and_7_out, not_1_out, not_2_out,
       not_3_out, not_4_out, not_5_out, not_6_out;

  not not_1 (not_1_out, add1);
  not not_2 (not_2_out, add2);
  not not_3 (not_3_out, add1);
  not not_4 (not_4_out, preflag);
  not not_5 (not_5_out, add2);
  not not_6 (not_6_out, preflag);
  and and_1 (and_1_out, add2, preflag);
  and and_2 (and_2_out, add1, preflag);
  and and_3 (and_3_out, add1, add2);
  and and_4 (and_4_out, not_1_out, not_2_out, preflag);
  and and_5 (and_5_out, not_3_out, add2, not_4_out);
  and and_6 (and_6_out, add1, not_5_out, not_6_out);
  and and_7 (and_7_out, add1, add2, preflag);
  or or_1 (flag, and_1_out, and_2_out, and_3_out);
  or or_2 (sum, and_4_out, and_5_out, and_6_out, and_7_out);
endmodule

module add_sub (
  input  [3:0] in_1,
  input  [3:0] in_2,
  input  sel,
  output [3:0] out_4
);

  wire [3:0] multiplexer_1_out, n4bitadder_1__4bitsum, not_1_out;

  assign not_1_out = ~in_2;  // NOT_Gate not_1, 4 bits wide
  _4bitadder u_4bitadder_1 (.in_1(not_1_out), .in_2(4'b0001), ._4bitsum(n4bitadder_1__4bitsum));  // open: output
  _4bitadder u_4bitadder_2 (.in_1(in_1), .in_2(multiplexer_1_out), ._4bitsum(out_4));  // open: output
  Multiplexer #(.width(4), .enable("false")) multiplexer_1 (
    .in0(in_2), .in1(n4bitadder_1__4bitsum), .out(multiplexer_1_out), .sel(sel));
endmodule

module ALU (
  input  [3:0] in_1,
  input  [3:0] in_2,
  input  [1:0] in_3,
  output [3:0] out_4
);

  wire [3:0] add_sub_1_out_4, and_1_out, or_1_out;

  add_sub add_sub_1 (.in_1(in_1), .in_2(in_2), .sel(in_3[0]), .out_4(add_sub_1_out_4));
  assign and_1_out = in_1 & in_2;  // AND_Gate and_1, 4 bits wide
  assign or_1_out = in_1 | in_2;  // OR_Gate or_1, 4 bits wide
  Multiplexer #(.select(2), .width(4), .enable("false")) multiplexer_1 (
    .in0(add_sub_1_out_4), .in1(add_sub_1_out_4), .in2(and_1_out), .in3(or_1_out), .out(out_4), .sel(in_3));
endmodule
