// Logisim project P0Q2Guess.circ as structural Verilog: 3 circuits, main circuit situationTransfer
module situationTransfer (
  input  [3:0] in_1,
  input  [1:0] in_2,
  output [3:0] out_3
);

  wire and_4_out, and_5_out, not_1_out, not_2_out, not_3_out, not_4_out, not_5_out, not_6_out;

  not not_1 (not_1_out, in_2[0]);
  not not_2 (not_2_out, in_2[0]);
  not not_3 (not_3_out, in_2[1]);
  not not_4 (not_4_out, in_1[2]);
  not not_5 (not_5_out, in_1[1]);
  not not_6 (not_6_out, in_2[0]);
  and and_1 (out_3[3], in_1[2], not_1_out);
  and and_2 (out_3[2], in_1[1], not_2_out);
  and and_3 (out_3[1], not_3_out, in_2[0]);
  and and_4 (and_4_out, not_4_out, not_5_out, not_6_out);
  or or_1 (out_3[0], and_4_out, and_5_out);
  and and_5 (and_5_out, in_2[1], in_2[0]);
endmodule

module fsm (
  input  in_1,
  input  [1:0] in_2,
  output out_3
);

  wire clock_1_out;
  wire [3:0] multiplexer_1_out, register_1_q, situationtransfer_1_out_3;

  situationTransfer situationtransfer_1 (.in_1(register_1_q), .in_2(in_2), .out_3(situationtransfer_1_out_3));
  Multiplexer #(.width(4), .enable("false")) multiplexer_1 (
    .in0(situationtransfer_1_out_3), .in1(4'b0000), .out(multiplexer_1_out), .sel(in_1));
  Register #(.width(4)) register_1 (.D(multiplexer_1_out), .Q(register_1_q), .clk(clock_1_out));  // open: en, clr
  Clock clock_1 (.out(clock_1_out));
  \output  output_1 (.in_1(in_2), .in_2(register_1_q), .o(out_3));

  // Other names for the same wires on the sheet: in[1:0] = in_2
endmodule

module \output  (
  input  [1:0] in_1,
  input  [3:0] in_2,
  output o
);

  wire not_1_out, not_2_out, not_3_out, not_4_out;

  not not_1 (not_1_out, in_1[0]);
  not not_2 (not_2_out, in_2[3]);
  not not_3 (not_3_out, in_2[1]);
  not not_4 (not_4_out, in_2[0]);
  and and_1 (o, not_1_out, not_2_out, in_2[2], not_3_out, not_4_out);
endmodule
