// Logisim project P0fsm.circ as structural Verilog: 2 circuits, main circuit fsm
module fsm (
  input  CLR,
  input  [1:0] In,
  output out_3
);

  wire clock_1_out, not_1_out, not_2_out;
  wire [1:0] multiplexer_1_out, register_1_q, \状态转移_out_3 ;

  Multiplexer #(.width(2), .enable("false")) multiplexer_1 (
    .in0(\状态转移_out_3 ), .in1(2'b00), .out(multiplexer_1_out), .sel(CLR));
  Register #(.width(2)) register_1 (.D(multiplexer_1_out), .Q(register_1_q), .clk(clock_1_out));  // open: en, clr
  Clock clock_1 (.out(clock_1_out));
  situationTransfer \u_状态转移  (.pre(register_1_q), .In(In), .out_3(\状态转移_out_3 ));
  not not_1 (not_1_out, register_1_q[0]);
  not not_2 (not_2_out, In[0]);
  and and_1 (out_3, not_1_out, register_1_q[1], not_2_out);
endmodule

module situationTransfer (
  input  [1:0] pre,
  input  [1:0] In,
  output [1:0] out_3
);

  wire and_1_out, and_2_out, and_3_out, and_4_out, not_1_out, not_2_out, not_3_out, not_4_out, not_5_out,
       not_6_out, not_7_out;

  not not_1 (not_1_out, In[1]);
  not not_2 (not_2_out, pre[0]);
  not not_3 (not_3_out, In[0]);
  not not_4 (not_4_out, pre[0]);
  not not_5 (not_5_out, In[0]);
  not not_6 (not_6_out, pre[1]);
  not not_7 (not_7_out, In[0]);
  and and_1 (and_1_out, In[0], not_1_out);
  and and_2 (and_2_out, not_2_out, pre[1], not_3_out);
  and and_3 (and_3_out, not_4_out, pre[1], not_5_out);
  and and_4 (and_4_out, pre[0], not_6_out, not_7_out);
  or or_1 (out_3[0], and_1_out, and_2_out);
  or or_2 (out_3[1], and_3_out, and_4_out);
endmodule
