// Logisim project P0fsmGuess.circ as structural Verilog: 3 circuits, main circuit fsm
module fsm (
  input  [1:0] In,
  input  CLR,
  output out_3
);

  wire clock_1_out;
  wire [1:0] multiplexer_1_out, \状态存储_q , \状态转移逻辑_out_3 ;

  situatinonTransfer \u_状态转移逻辑  (.pre(\状态存储_q ), .in(In), .out_3(\状态转移逻辑_out_3 ));
  Multiplexer #(.width(2), .enable("false")) multiplexer_1 (
    .in0(\状态转移逻辑_out_3 ), .in1(2'b00), .out(multiplexer_1_out), .sel(CLR));
  Register #(.width(2)) \u_状态存储  (.D(multiplexer_1_out), .Q(\状态存储_q ), .clk(clock_1_out));  // open: en, clr
  Clock clock_1 (.out(clock_1_out));
  \output  \u_输出逻辑  (.in(In), .s(\状态存储_q ), .o(out_3));
endmodule

module situatinonTransfer (
  input  [1:0] pre,
  input  [1:0] in,
  output [1:0] out_3
);

  wire not_1_out, not_2_out;

  not not_1 (not_1_out, in[0]);
  not not_2 (not_2_out, in[1]);
  and and_1 (out_3[1], pre[0], not_1_out);
  and and_2 (out_3[0], not_2_out, in[0]);
endmodule

module \output  (
  input  [1:0] in,
  input  [1:0] s,
  output o
);

  wire not_1_out, not_2_out;

  not not_1 (not_1_out, in[0]);
  not not_2 (not_2_out, s[0]);
  and and_1 (o, not_1_out, s[1], not_2_out);
endmodule
