// Logisim project SR.circ as structural Verilog: 2 circuits, main circuit SR_1
module SR_1 (
  input  R,
  input  S,
  output Q,
  output nQ
);

  wire or_1_out, or_2_out;

  or or_1 (or_1_out, R, nQ);
  or or_2 (or_2_out, Q, S);
  not not_1 (Q, or_1_out);
  not not_2 (nQ, or_2_out);
endmodule

module SR_2 (
  input  in_1,
  input  in_2,
  output out_3,
  output out_4
);

  wire not_1_out, not_2_out;

  not not_1 (not_1_out, in_1);
  not not_2 (not_2_out, in_2);
  nand nand_1 (out_3, not_1_out, out_4);
  nand nand_2 (out_4, out_3, not_2_out);
endmodule
