// Logisim project all_add.circ as structural Verilog: 1 circuit, main circuit main
module main (
  input  A,
  input  B,
  input  C,
  output F1,
  output F2
);

  wire and_1_out, and_2_out, and_3_out, and_4_out, or_1_out, or_2_out;

  and and_1 (and_1_out, A, B);
  or or_1 (or_1_out, B, A);
  and and_2 (and_2_out, or_1_out, C);
  or or_2 (or_2_out, or_1_out, C);
  and and_3 (and_3_out, and_1_out, C);
  or or_3 (F1, and_1_out, and_2_out);
  and and_4 (and_4_out, ~F1, or_2_out);  // AND_Gate
  or or_4 (F2, and_4_out, and_3_out);
endmodule
