// Logisim project choice.circ as structural Verilog: 1 circuit, main circuit main
module main (
  input  A,
  input  B,
  input  C,
  input  D,
  input  [1:0] in_5
);

  wire decoder_1_out0, decoder_1_out1, decoder_1_out2, decoder_1_out3, multiplexer_1_out;

  LED led_1 (.in(multiplexer_1_out));
  Multiplexer #(.select(2)) multiplexer_1 (
    .in0(A), .in1(B), .in2(C), .in3(D), .out(multiplexer_1_out), .sel(in_5));  // open: en
  Decoder #(.select(2)) decoder_1 (
    .out0(decoder_1_out0), .out1(decoder_1_out1), .out2(decoder_1_out2), .out3(decoder_1_out3), .sel(in_5));  // open: en
  LED u_A (.in(decoder_1_out0));
  LED u_B (.in(decoder_1_out1));
  LED u_C (.in(decoder_1_out2));
  LED u_D (.in(decoder_1_out3));

  // Notes on the sheet:
  //   B: pull=up
endmodule
