// Logisim project fiblogn.circ as structural Verilog: 4 circuits, main circuit main
module main (
  input  [31:0] in_1,
  output [31:0] out_2
);

  wire and_1_out, bitselector_1_out, clock_1_out, comparator_1_eq, comparator_1_lt, initial_1_out_2,
       initial_2_out_2, initial_3_out_2, initial_4_out_2, multiplexer_7_out, multiplexer_8_out, undriven;
  wire [31:0] multi_1_out_9, multi_1_out_10, multi_1_out_11, multi_1_out_12, multi_2_out_9, multi_2_out_10,
       multi_2_out_11, multi_2_out_12, multiplexer_1_out, multiplexer_2_out, multiplexer_3_out,
       multiplexer_4_out, multiplexer_5_out, multiplexer_6_out, n4reg_1_out_6, n4reg_1_out_7, n4reg_1_out_8,
       n4reg_1_out_9, n4reg_2_out_6, n4reg_2_out_7, n4reg_2_out_8, n4reg_2_out_9, register_1_q,
       shifter_1_out, subtractor_1_out;

  Subtractor #(.width(32)) subtractor_1 (.a(in_1), .b(32'h1), .out(subtractor_1_out));  // open: bin, bout
  Multiplexer #(.width(32), .enable("false")) multiplexer_1 (
    .in0(subtractor_1_out), .in1(shifter_1_out), .out(multiplexer_1_out), .sel(initial_1_out_2));
  \initial  initial_1 (.out_2(initial_1_out_2), .in_1(register_1_q));
  Register #(.width(32)) register_1 (
    .D(multiplexer_1_out), .en(undriven), .Q(register_1_q), .clk(clock_1_out));  // open: clr
  Clock clock_1 (.out(clock_1_out));
  Shifter #(.width(32), .shift("lr")) shifter_1 (.in(register_1_q), .\dist (5'b00001), .out(shifter_1_out));
  \initial  initial_2 (.out_2(initial_2_out_2), .in_1(register_1_q));
  Comparator #(.width(32), .mode("unsigned")) comparator_1 (
    .a({32{1'b0}}), .b(register_1_q), .eq(comparator_1_eq), .lt(comparator_1_lt));  // open: gt
  BitSelector #(.width(32)) bitselector_1 (.in(register_1_q), .out(bitselector_1_out), .sel({5{1'b0}}));
  and and_1 (and_1_out, comparator_1_lt, bitselector_1_out);
  Multiplexer #(.width(32), .enable("false")) multiplexer_2 (
    .in0(32'h1), .in1(multi_2_out_9), .out(multiplexer_2_out), .sel(initial_3_out_2));
  Multiplexer #(.width(32), .enable("false")) multiplexer_3 (
    .in0(32'h1), .in1(multi_1_out_12), .out(multiplexer_3_out), .sel(initial_4_out_2));
  Multiplexer #(.width(32), .enable("false")) multiplexer_4 (
    .in0(32'h1), .in1(multi_2_out_10), .out(multiplexer_4_out), .sel(initial_3_out_2));
  Multiplexer #(.width(32), .enable("false")) multiplexer_5 (
    .in0(32'h1), .in1(multi_2_out_11), .out(multiplexer_5_out), .sel(initial_3_out_2));
  Multiplexer #(.width(32), .enable("false")) multiplexer_6 (
    .in0(32'h1), .in1(multi_1_out_9), .out(multiplexer_6_out), .sel(initial_4_out_2));
  \initial  initial_3 (.out_2(initial_3_out_2), .in_1(n4reg_1_out_6));
  _4reg u_4reg_1 (
    .in_1(multiplexer_2_out), .in_2(multiplexer_4_out), .in_3(multiplexer_5_out), .in_4(multi_2_out_12),
    .in_5(multiplexer_7_out), .out_6(n4reg_1_out_6), .out_7(n4reg_1_out_7), .out_8(n4reg_1_out_8),
    .out_9(n4reg_1_out_9));
  Multiplexer #(.enable("false")) multiplexer_7 (
    .in0(1'b1), .in1(comparator_1_lt), .out(multiplexer_7_out), .sel(initial_2_out_2));
  \initial  initial_4 (.out_2(initial_4_out_2), .in_1(n4reg_2_out_6));
  _4reg u_4reg_2 (
    .in_1(multiplexer_6_out), .in_2(multi_1_out_10), .in_3(multi_1_out_11), .in_4(multiplexer_3_out),
    .in_5(multiplexer_8_out), .out_6(n4reg_2_out_6), .out_7(n4reg_2_out_7), .out_8(n4reg_2_out_8),
    .out_9(n4reg_2_out_9));
  Multiplexer #(.enable("false")) multiplexer_8 (
    .in0(1'b1), .in1(and_1_out), .out(multiplexer_8_out), .sel(initial_4_out_2));
  multi multi_1 (
    .in_1(n4reg_2_out_6), .in_2(n4reg_2_out_7), .in_3(n4reg_2_out_8), .in_4(n4reg_2_out_9),
    .in_5(n4reg_1_out_6), .in_6(n4reg_1_out_7), .in_7(n4reg_1_out_8), .in_8(n4reg_1_out_9),
    .out_9(multi_1_out_9), .out_10(multi_1_out_10), .out_11(multi_1_out_11), .out_12(multi_1_out_12));
  multi multi_2 (
    .in_1(n4reg_1_out_6), .in_2(n4reg_1_out_7), .in_3(n4reg_1_out_8), .in_4(n4reg_1_out_9),
    .in_5(n4reg_1_out_6), .in_6(n4reg_1_out_7), .in_7(n4reg_1_out_8), .in_8(n4reg_1_out_9),
    .out_9(multi_2_out_9), .out_10(multi_2_out_10), .out_11(multi_2_out_11), .out_12(multi_2_out_12));
  Multiplexer #(.width(32), .enable("false")) multiplexer_9 (
    .in0({32{1'b0}}), .in1(n4reg_2_out_6), .out(out_2), .sel(comparator_1_eq));
endmodule

module multi (
  input  [31:0] in_1,
  input  [31:0] in_2,
  input  [31:0] in_3,
  input  [31:0] in_4,
  input  [31:0] in_5,
  input  [31:0] in_6,
  input  [31:0] in_7,
  input  [31:0] in_8,
  output [31:0] out_9,
  output [31:0] out_10,
  output [31:0] out_11,
  output [31:0] out_12
);

  wire [31:0] multiplier_1_out, multiplier_2_out, multiplier_3_out, multiplier_4_out, multiplier_5_out,
       multiplier_6_out, multiplier_7_out, multiplier_8_out;

  Multiplier #(.width(32)) multiplier_1 (.a(in_1), .b(in_5), .out(multiplier_1_out));  // open: cin, cout
  Multiplier #(.width(32)) multiplier_2 (.a(in_2), .b(in_7), .out(multiplier_2_out));  // open: cin, cout
  Multiplier #(.width(32)) multiplier_3 (.a(in_1), .b(in_6), .out(multiplier_3_out));  // open: cin, cout
  Multiplier #(.width(32)) multiplier_4 (.a(in_2), .b(in_8), .out(multiplier_4_out));  // open: cin, cout
  Multiplier #(.width(32)) multiplier_5 (.a(in_3), .b(in_5), .out(multiplier_5_out));  // open: cin, cout
  Multiplier #(.width(32)) multiplier_6 (.a(in_4), .b(in_7), .out(multiplier_6_out));  // open: cin, cout
  Multiplier #(.width(32)) multiplier_7 (.a(in_3), .b(in_6), .out(multiplier_7_out));  // open: cin, cout
  Multiplier #(.width(32)) multiplier_8 (.a(in_4), .b(in_8), .out(multiplier_8_out));  // open: cin, cout
  Adder #(.width(32)) adder_1 (.a(multiplier_1_out), .b(multiplier_2_out), .out(out_9));  // open: cin, cout
  Adder #(.width(32)) adder_2 (.a(multiplier_3_out), .b(multiplier_4_out), .out(out_10));  // open: cin, cout
  Adder #(.width(32)) adder_3 (.a(multiplier_5_out), .b(multiplier_6_out), .out(out_11));  // open: cin, cout
  Adder #(.width(32)) adder_4 (.a(multiplier_7_out), .b(multiplier_8_out), .out(out_12));  // open: cin, cout
endmodule

module _4reg (
  input  [31:0] in_1,
  input  [31:0] in_2,
  input  [31:0] in_3,
  input  [31:0] in_4,
  input  in_5,
  output [31:0] out_6,
  output [31:0] out_7,
  output [31:0] out_8,
  output [31:0] out_9
);

  wire clock_1_out;

  Register #(.width(32)) register_1 (.D(in_1), .en(in_5), .Q(out_6), .clk(clock_1_out));  // open: clr
  Register #(.width(32)) register_2 (.D(in_2), .en(in_5), .Q(out_7), .clk(clock_1_out));  // open: clr
  Register #(.width(32)) register_3 (.D(in_3), .en(in_5), .Q(out_8), .clk(clock_1_out));  // open: clr
  Register #(.width(32)) register_4 (.D(in_4), .en(in_5), .Q(out_9), .clk(clock_1_out));  // open: clr
  Clock clock_1 (.out(clock_1_out));
endmodule

module \initial  (
  input  [31:0] in_1,
  output out_2
);

  or or_1 (out_2, in_1[0], in_1[1], in_1[2], in_1[3], in_1[4], in_1[5], in_1[6], in_1[7], in_1[8], in_1[9], in_1[10], in_1[11], in_1[12], in_1[13], in_1[14], in_1[15], in_1[16], in_1[17], in_1[18], in_1[19], in_1[20], in_1[21], in_1[22], in_1[23], in_1[24], in_1[25], in_1[26], in_1[27], in_1[28], in_1[29], in_1[30], in_1[31]);
endmodule
