// Logisim project fibonacci.circ as structural Verilog: 1 circuit, main circuit main
module main (
  input  [2:0] in_1,
  output [3:0] out_2
);

  wire clock_1_out, comparator_1_eq, comparator_2_eq, comparator_2_lt, or_1_out;
  wire [2:0] adder_2_out;
  wire [3:0] adder_1_out, d_ff_1_q, multiplexer_1_out, register_1_q_2;
  wire [14:0] register_1_q;

  or or_1 (or_1_out, register_1_q[14], register_1_q[13], register_1_q[12]);
  Comparator #(.width(3), .mode("unsigned")) comparator_1 (.a(in_1), .b(3'b001), .eq(comparator_1_eq));  // open: gt, lt
  Multiplexer #(.width(4), .enable("false")) multiplexer_1 (
    .in0(4'b0001), .in1(register_1_q[11:8]), .out(multiplexer_1_out), .sel(or_1_out));
  Adder #(.width(4)) adder_1 (.a(register_1_q_2), .b(multiplexer_1_out), .out(adder_1_out));  // open: cin, cout
  Adder #(.width(3)) adder_2 (.a(register_1_q[14:12]), .b(3'b001), .out(adder_2_out));  // open: cin, cout
  Comparator #(.width(3), .mode("unsigned")) comparator_2 (
    .a(adder_2_out), .b(in_1), .eq(comparator_2_eq), .lt(comparator_2_lt));  // open: gt
  Register #(.width(15)) register_1 (
    .D({adder_2_out, adder_1_out, multiplexer_1_out, adder_1_out}), .en(comparator_2_lt),
    .Q({register_1_q[14:8], register_1_q_2, register_1_q[3:0]}), .clk(clock_1_out));  // open: clr
  Clock clock_1 (.out(clock_1_out));
  D_Flip_Flop d_ff_1 (
    .clk(clock_1_out), .D(register_1_q[0]), .Q(d_ff_1_q[0]), .en(comparator_2_eq));  // open: Qn, preset, reset
  D_Flip_Flop d_ff_2 (
    .clk(clock_1_out), .D(register_1_q[1]), .Q(d_ff_1_q[1]), .en(comparator_2_eq));  // open: Qn, preset, reset
  D_Flip_Flop d_ff_3 (
    .clk(clock_1_out), .D(register_1_q[2]), .Q(d_ff_1_q[2]), .en(comparator_2_eq));  // open: Qn, preset, reset
  D_Flip_Flop d_ff_4 (
    .clk(clock_1_out), .D(register_1_q[3]), .Q(d_ff_1_q[3]), .en(comparator_2_eq));  // open: Qn, preset, reset
  Multiplexer #(.width(4), .enable("false")) multiplexer_2 (
    .in0(d_ff_1_q), .in1(4'b0001), .out(out_2), .sel(comparator_1_eq));
endmodule
