// Logisim project first_of_all.circ as structural Verilog: 1 circuit, main circuit main
module main (
  input  x,
  input  y,
  input  [5:0] in_3,
  output out_4
);

  wire and_1_out, and_2_out, not_1_out, not_2_out;
  wire [2:0] or_1_out;

  not not_1 (not_1_out, x);
  not not_2 (not_2_out, y);
  assign or_1_out = in_3[2:0] | in_3[5:3];  // OR_Gate or_1, 3 bits wide
  and and_1 (and_1_out, not_1_out, y);
  and and_2 (and_2_out, x, not_2_out);
  // Probe on or_1_out
  or or_2 (out_4, and_1_out, and_2_out);
endmodule
