// Logisim project mod5.circ as structural Verilog
module mod5 (
  input  In,
  output out_2,
  output out_3,
  output out_4,
  output out_5,
  output out_6
);

  wire clock_1_out, nor_1_out, nor_2_out, not_1_out, not_2_out, not_3_out, not_4_out, or_1_out, or_2_out,
       or_3_out, or_4_out;
  wire [4:1] and_1_out, register_1_q;

  nor nor_1 (nor_1_out, out_2, register_1_q[1], register_1_q[2], register_1_q[3], register_1_q[4]);
  not not_1 (not_1_out, In);
  or or_1 (or_1_out, nor_1_out, out_2, register_1_q[1], register_1_q[4]);
  and and_1 (and_1_out[1], or_1_out, not_1_out);
  and and_2 (and_1_out[2], or_1_out, In);
  or or_2 (or_2_out, register_1_q[2], register_1_q[3]);
  and and_3 (and_1_out[3], or_2_out, In);
  and and_4 (and_1_out[4], or_2_out, not_2_out);
  not not_2 (not_2_out, In);
  Register #(.width(5)) register_1 (
    .D({and_1_out, 1'b0}), .Q({register_1_q, out_2}), .clk(clock_1_out));  // open: en, clr
  Clock clock_1 (.out(clock_1_out));
  nor nor_2 (nor_2_out, out_2, register_1_q[1], register_1_q[2], register_1_q[3], register_1_q[4]);
  or or_3 (or_3_out, nor_2_out, register_1_q[1], register_1_q[4]);
  not not_3 (not_3_out, In);
  or or_4 (or_4_out, register_1_q[2], register_1_q[3]);
  not not_4 (not_4_out, In);
  and and_5 (out_3, or_3_out, not_3_out);
  and and_6 (out_4, or_3_out, In);
  and and_7 (out_5, or_4_out, In);
  and and_8 (out_6, or_4_out, not_4_out);
endmodule
