// Logisim project sort.circ as structural Verilog: 3 circuits, main circuit 1bit_swap
module _1bit_swap (
  input  l1,
  input  l2,
  input  ctr,
  output o1,
  output o2
);

  wire and_1_out, and_2_out, and_3_out, and_4_out, not_1_out, not_2_out;

  not not_1 (not_1_out, ctr);
  not not_2 (not_2_out, ctr);
  and and_1 (and_1_out, l2, ctr);
  and and_2 (and_2_out, l1, not_1_out);
  and and_3 (and_3_out, l2, not_2_out);
  and and_4 (and_4_out, l1, ctr);
  or or_1 (o1, and_1_out, and_2_out);
  or or_2 (o2, and_3_out, and_4_out);
endmodule

module _4bit_swap (
  input  in_1,
  input  [3:0] in4b_1,
  input  [3:0] in4b_2,
  output [3:0] o4b_1,
  output [3:0] o4b_2
);

  _1bit_swap u_1bit_swap_1 (.l1(in4b_1[0]), .l2(in4b_2[0]), .ctr(in_1), .o1(o4b_1[0]), .o2(o4b_2[0]));
  _1bit_swap u_1bit_swap_2 (.l1(in4b_1[1]), .l2(in4b_2[1]), .ctr(in_1), .o1(o4b_1[1]), .o2(o4b_2[1]));
  _1bit_swap u_1bit_swap_3 (.l1(in4b_1[2]), .l2(in4b_2[2]), .ctr(in_1), .o1(o4b_1[2]), .o2(o4b_2[2]));
  _1bit_swap u_1bit_swap_4 (.l1(in4b_1[3]), .l2(in4b_2[3]), .ctr(in_1), .o1(o4b_1[3]), .o2(o4b_2[3]));
endmodule

module _4bit_sort (
  input  [3:0] in_1,
  input  [3:0] in_2,
  input  [3:0] in_3,
  input  [3:0] in_4,
  output [3:0] out_5,
  output [3:0] out_6,
  output [3:0] out_7,
  output [3:0] out_8
);

  wire comparator_1_gt, comparator_2_gt, comparator_3_gt, comparator_4_gt, comparator_5_gt, comparator_6_gt;
  wire [3:0] _1, _2, _3, n4bit_swap_1_o4b_2, n4bit_swap_2_o4b_2, n4bit_swap_3_o4b_1, n4bit_swap_3_o4b_2,
       n4bit_swap_4_o4b_1;

  Comparator #(.width(4), .mode("unsigned")) comparator_1 (.a(in_1), .b(in_2), .gt(comparator_1_gt));  // open: eq, lt
  _4bit_swap u_4bit_swap_1 (
    .in4b_1(in_1), .in4b_2(in_2), .in_1(comparator_1_gt), .o4b_1(_1), .o4b_2(n4bit_swap_1_o4b_2));
  Comparator #(.width(4), .mode("unsigned")) comparator_2 (.a(_1), .b(_2), .gt(comparator_2_gt));  // open: eq, lt
  Comparator #(.width(4), .mode("unsigned")) comparator_3 (
    .a(n4bit_swap_1_o4b_2), .b(in_3), .gt(comparator_3_gt));  // open: eq, lt
  _4bit_swap u_4bit_swap_2 (
    .in4b_1(n4bit_swap_1_o4b_2), .in4b_2(in_3), .in_1(comparator_3_gt), .o4b_1(_2), .o4b_2(n4bit_swap_2_o4b_2));
  _4bit_swap u_4bit_swap_3 (
    .in4b_1(_1), .in4b_2(_2), .in_1(comparator_2_gt), .o4b_1(n4bit_swap_3_o4b_1), .o4b_2(n4bit_swap_3_o4b_2));
  Comparator #(.width(4), .mode("unsigned")) comparator_4 (
    .a(n4bit_swap_2_o4b_2), .b(in_4), .gt(comparator_4_gt));  // open: eq, lt
  Comparator #(.width(4), .mode("unsigned")) comparator_5 (
    .a(n4bit_swap_3_o4b_2), .b(_3), .gt(comparator_5_gt));  // open: eq, lt
  _4bit_swap u_4bit_swap_4 (
    .in4b_1(n4bit_swap_3_o4b_2), .in4b_2(_3), .in_1(comparator_5_gt), .o4b_1(n4bit_swap_4_o4b_1),
    .o4b_2(out_7));
  _4bit_swap u_4bit_swap_5 (
    .in4b_1(n4bit_swap_2_o4b_2), .in4b_2(in_4), .in_1(comparator_4_gt), .o4b_1(_3), .o4b_2(out_8));
  Comparator #(.width(4), .mode("unsigned")) comparator_6 (
    .a(n4bit_swap_3_o4b_1), .b(n4bit_swap_4_o4b_1), .gt(comparator_6_gt));  // open: eq, lt
  _4bit_swap u_4bit_swap_6 (
    .in4b_1(n4bit_swap_3_o4b_1), .in4b_2(n4bit_swap_4_o4b_1), .in_1(comparator_6_gt), .o4b_1(out_5),
    .o4b_2(out_6));

  // Other names for the same wires on the sheet: _3_2[3:0] = out_7; _4[3:0] = out_8
endmodule
