// Logisim project superFib.circ as structural Verilog: 3 circuits, main circuit main
module main (
  input  [31:0] in_1,
  output [31:0] out_2
);

  wire clock_1_out, comparator_1_eq, comparator_2_eq, comparator_2_lt, n32split_or_1_out_2;
  wire [31:0] adder_1_out, adder_2_out, multiplexer_1_out, n32bdff_1_out_3, register_1_q, register_2_q,
       register_3_q, register_4_q;

  _32split_or u_32split_or_1 (.in_1(register_4_q), .out_2(n32split_or_1_out_2));
  Comparator #(.width(32), .mode("unsigned")) comparator_1 (.a(in_1), .b(32'h1), .eq(comparator_1_eq));  // open: gt, lt
  Adder #(.width(32)) adder_1 (.a(register_4_q), .b(32'h1), .out(adder_1_out));  // open: cin, cout
  Multiplexer #(.width(32), .enable("false")) multiplexer_1 (
    .in0(32'h1), .in1(register_3_q), .out(multiplexer_1_out), .sel(n32split_or_1_out_2));
  Comparator #(.width(32), .mode("unsigned")) comparator_2 (
    .a(adder_1_out), .b(in_1), .eq(comparator_2_eq), .lt(comparator_2_lt));  // open: gt
  Adder #(.width(32)) adder_2 (.a(register_2_q), .b(multiplexer_1_out), .out(adder_2_out));  // open: cin, cout
  Register #(.width(32)) register_1 (
    .D(adder_2_out), .en(comparator_2_lt), .Q(register_1_q), .clk(clock_1_out));  // open: clr
  Register #(.width(32)) register_2 (
    .D(multiplexer_1_out), .en(comparator_2_lt), .Q(register_2_q), .clk(clock_1_out));  // open: clr
  Register #(.width(32)) register_3 (
    .D(adder_2_out), .en(comparator_2_lt), .Q(register_3_q), .clk(clock_1_out));  // open: clr
  Register #(.width(32)) register_4 (
    .D(adder_1_out), .en(comparator_2_lt), .Q(register_4_q), .clk(clock_1_out));  // open: clr
  Clock clock_1 (.out(clock_1_out));
  _32bDFF u_32bdff_1 (.in_1(register_1_q), .in_2(comparator_2_eq), .out_3(n32bdff_1_out_3));
  Multiplexer #(.width(32), .enable("false")) multiplexer_2 (
    .in0(n32bdff_1_out_3), .in1(32'h1), .out(out_2), .sel(comparator_1_eq));
endmodule

module _32split_or (
  input  [31:0] in_1,
  output out_2
);

  or or_1 (out_2, in_1[31], in_1[30], in_1[29], in_1[28], in_1[27], in_1[26], in_1[25], in_1[24], in_1[23], in_1[22], in_1[21], in_1[20], in_1[19], in_1[18], in_1[17], in_1[16], in_1[15], in_1[14], in_1[13], in_1[12], in_1[11], in_1[10], in_1[9], in_1[8], in_1[7], in_1[6], in_1[5], in_1[4], in_1[3], in_1[2], in_1[1], in_1[0]);
endmodule

module _32bDFF (
  input  [31:0] in_1,
  input  in_2,
  output [31:0] out_3
);

  wire clock_1_out;

  Clock clock_1 (.out(clock_1_out));
  D_Flip_Flop d_ff_1 (.clk(clock_1_out), .D(in_1[0]), .Q(out_3[0]), .en(in_2));  // open: Qn, preset, reset
  D_Flip_Flop d_ff_2 (.clk(clock_1_out), .D(in_1[1]), .Q(out_3[1]), .en(in_2));  // open: Qn, preset, reset
  D_Flip_Flop d_ff_3 (.clk(clock_1_out), .D(in_1[2]), .Q(out_3[2]), .en(in_2));  // open: Qn, preset, reset
  D_Flip_Flop d_ff_4 (.clk(clock_1_out), .D(in_1[3]), .Q(out_3[3]), .en(in_2));  // open: Qn, preset, reset
  D_Flip_Flop d_ff_5 (.clk(clock_1_out), .D(in_1[4]), .Q(out_3[4]), .en(in_2));  // open: Qn, preset, reset
  D_Flip_Flop d_ff_6 (.clk(clock_1_out), .D(in_1[5]), .Q(out_3[5]), .en(in_2));  // open: Qn, preset, reset
  D_Flip_Flop d_ff_7 (.clk(clock_1_out), .D(in_1[6]), .Q(out_3[6]), .en(in_2));  // open: Qn, preset, reset
  D_Flip_Flop d_ff_8 (.clk(clock_1_out), .D(in_1[7]), .Q(out_3[7]), .en(in_2));  // open: Qn, preset, reset
  D_Flip_Flop d_ff_9 (.clk(clock_1_out), .D(in_1[8]), .Q(out_3[8]), .en(in_2));  // open: Qn, preset, reset
  D_Flip_Flop d_ff_10 (.clk(clock_1_out), .D(in_1[9]), .Q(out_3[9]), .en(in_2));  // open: Qn, preset, reset
  D_Flip_Flop d_ff_11 (.clk(clock_1_out), .D(in_1[10]), .Q(out_3[10]), .en(in_2));  // open: Qn, preset, reset
  D_Flip_Flop d_ff_12 (.clk(clock_1_out), .D(in_1[11]), .Q(out_3[11]), .en(in_2));  // open: Qn, preset, reset
  D_Flip_Flop d_ff_13 (.clk(clock_1_out), .D(in_1[12]), .Q(out_3[12]), .en(in_2));  // open: Qn, preset, reset
  D_Flip_Flop d_ff_14 (.clk(clock_1_out), .D(in_1[13]), .Q(out_3[13]), .en(in_2));  // open: Qn, preset, reset
  D_Flip_Flop d_ff_15 (.clk(clock_1_out), .D(in_1[14]), .Q(out_3[14]), .en(in_2));  // open: Qn, preset, reset
  D_Flip_Flop d_ff_16 (.clk(clock_1_out), .D(in_1[15]), .Q(out_3[15]), .en(in_2));  // open: Qn, preset, reset
  D_Flip_Flop d_ff_17 (.clk(clock_1_out), .D(in_1[16]), .Q(out_3[16]), .en(in_2));  // open: Qn, preset, reset
  D_Flip_Flop d_ff_18 (.clk(clock_1_out), .D(in_1[17]), .Q(out_3[17]), .en(in_2));  // open: Qn, preset, reset
  D_Flip_Flop d_ff_19 (.clk(clock_1_out), .D(in_1[18]), .Q(out_3[18]), .en(in_2));  // open: Qn, preset, reset
  D_Flip_Flop d_ff_20 (.clk(clock_1_out), .D(in_1[19]), .Q(out_3[19]), .en(in_2));  // open: Qn, preset, reset
  D_Flip_Flop d_ff_21 (.clk(clock_1_out), .D(in_1[20]), .Q(out_3[20]), .en(in_2));  // open: Qn, preset, reset
  D_Flip_Flop d_ff_22 (.clk(clock_1_out), .D(in_1[21]), .Q(out_3[21]), .en(in_2));  // open: Qn, preset, reset
  D_Flip_Flop d_ff_23 (.clk(clock_1_out), .D(in_1[22]), .Q(out_3[22]), .en(in_2));  // open: Qn, preset, reset
  D_Flip_Flop d_ff_24 (.clk(clock_1_out), .D(in_1[23]), .Q(out_3[23]), .en(in_2));  // open: Qn, preset, reset
  D_Flip_Flop d_ff_25 (.clk(clock_1_out), .D(in_1[24]), .Q(out_3[24]), .en(in_2));  // open: Qn, preset, reset
  D_Flip_Flop d_ff_26 (.clk(clock_1_out), .D(in_1[25]), .Q(out_3[25]), .en(in_2));  // open: Qn, preset, reset
  D_Flip_Flop d_ff_27 (.clk(clock_1_out), .D(in_1[26]), .Q(out_3[26]), .en(in_2));  // open: Qn, preset, reset
  D_Flip_Flop d_ff_28 (.clk(clock_1_out), .D(in_1[27]), .Q(out_3[27]), .en(in_2));  // open: Qn, preset, reset
  D_Flip_Flop d_ff_29 (.clk(clock_1_out), .D(in_1[28]), .Q(out_3[28]), .en(in_2));  // open: Qn, preset, reset
  D_Flip_Flop d_ff_30 (.clk(clock_1_out), .D(in_1[29]), .Q(out_3[29]), .en(in_2));  // open: Qn, preset, reset
  D_Flip_Flop d_ff_31 (.clk(clock_1_out), .D(in_1[30]), .Q(out_3[30]), .en(in_2));  // open: Qn, preset, reset
  D_Flip_Flop d_ff_32 (.clk(clock_1_out), .D(in_1[31]), .Q(out_3[31]), .en(in_2));  // open: Qn, preset, reset
endmodule
