// Logisim project swap.circ as structural Verilog: 1 circuit, main circuit main
module main (
  input  L1,
  input  L2,
  input  Ctr,
  output O1,
  output O2
);

  wire not_1_out, not_2_out, not_3_out, not_4_out, not_5_out, not_6_out, not_7_out, or_1_out, or_2_out,
       or_3_out, or_4_out, or_5_out, or_6_out;

  not not_1 (not_1_out, L1);
  not not_2 (not_2_out, Ctr);
  not not_3 (not_3_out, L2);
  not not_4 (not_4_out, Ctr);
  not not_5 (not_5_out, L1);
  not not_6 (not_6_out, L2);
  not not_7 (not_7_out, Ctr);
  or or_1 (or_1_out, not_1_out, L2, not_2_out);
  or or_2 (or_2_out, L1, not_3_out, Ctr);
  or or_3 (or_3_out, L1, L2, Ctr);
  or or_4 (or_4_out, L1, L2, not_4_out);
  or or_5 (or_5_out, not_5_out, L2, Ctr);
  or or_6 (or_6_out, L1, not_6_out, not_7_out);
  and and_1 (O1, or_1_out, or_2_out, or_3_out, or_4_out);
  and and_2 (O2, or_3_out, or_4_out, or_5_out, or_6_out);
endmodule
