// Logisim project CPUv3.circ as structural Verilog: 10 circuits, main circuit ALU
module main (
  input  in_1,
  output [31:0] out_2,
  output out_3,
  output [4:0] out_4,
  output [31:0] out_5,
  output out_6,
  output [4:0] out_7,
  output [31:0] out_8
);

  wire ALU_out_4, ALU_out_5, ALU_out_6, BCtr, clock_1_out, WACtr;
  wire [1:0] Controller_brctr, EXTCtr, WDCtr;
  wire [2:0] ALUCtr;
  wire [4:0] Decoder_rd, Decoder_rs, Decoder_rt;
  wire [5:0] Decoder_func, Decoder_op;
  wire [15:0] Decoder_imm;
  wire [31:0] ALU_aluout, DM_data, EXT_extout, multiplexer_3_out, RF_out_8, subtractor_1_out;

  IFU IFU (
    .Br(Controller_brctr), .equal(ALU_out_5), .less(ALU_out_6), .greater(ALU_out_4), .in_5(clock_1_out),
    .rst(in_1), .out_7(out_2));
  Decoder Decoder (
    .in_1(out_2), .op(Decoder_op), .rs(Decoder_rs), .rt(Decoder_rt), .rd(Decoder_rd), .func(Decoder_func),
    .Imm(Decoder_imm));  // open: shamt
  Multiplexer #(.width(5), .enable("false")) multiplexer_1 (
    .in0(Decoder_rd), .in1(Decoder_rt), .out(out_4), .sel(WACtr));
  Multiplexer #(.select(2), .width(32), .enable("false")) multiplexer_2 (
    .in0(ALU_aluout), .in1(DM_data), .in2(EXT_extout), .out(out_5), .sel(WDCtr));  // open: in3
  EXT EXT (.Imm(Decoder_imm), .EXTCtr(EXTCtr), .ExtOut(EXT_extout));
  Clock clock_1 (.out(clock_1_out));
  RF RF (
    .RA1(Decoder_rs), .RA2(Decoder_rt), .WA(out_4), .WD(out_5), .in_1(out_3), .clk(clock_1_out), .rst(in_1),
    .out_8(RF_out_8), .out_9(out_8));
  Multiplexer #(.width(32), .enable("false")) multiplexer_3 (
    .in0(out_8), .in1(EXT_extout), .out(multiplexer_3_out), .sel(BCtr));
  Controller Controller (
    .op(Decoder_op), .func(Decoder_func), .WACtr(WACtr), .WDCtr(WDCtr), .EXTCtr(EXTCtr), .BCtr(BCtr),
    .ALUCtr(ALUCtr), .MemWrite(out_6), .WE(out_3), .BrCtr(Controller_brctr));
  ALU ALU (
    .A(RF_out_8), .B(multiplexer_3_out), .ALUCtr(ALUCtr), .ALUOut(ALU_aluout), .out_5(ALU_out_5),
    .out_6(ALU_out_6), .out_4(ALU_out_4));
  Subtractor #(.width(32)) subtractor_1 (
    .a(ALU_aluout), .b(32'h2000), .out({subtractor_1_out[31:7], out_7, subtractor_1_out[1:0]}));  // open: bin, bout
  DM DM (.MemAddr(out_7), .wd(out_8), .clk(clock_1_out), .rst(in_1), .MemWrite(out_6), .data(DM_data));

  // Other names for the same wires on the sheet: MemAddr[4:0] = out_7; Instr[31:0] = out_2; MemData[31:0] = out_8;
  //   MemWrite = out_6; RegAddr[4:0] = out_4; RegData[31:0] = out_5; RegWrite = out_3; Reset = in_1
endmodule

module ALU (
  input  [31:0] A,
  input  [31:0] B,
  input  [2:0] ALUCtr,
  output out_4,
  output out_5,
  output out_6,
  output [31:0] ALUOut
);

  wire [31:0] adder_1_out, or_1_out, subtractor_1_out;

  Comparator #(.width(32)) comparator_1 (.a(A), .b(B), .gt(out_4), .eq(out_5), .lt(out_6));
  Adder #(.width(32)) adder_1 (.a(A), .b(B), .out(adder_1_out));  // open: cin, cout
  Subtractor #(.width(32)) subtractor_1 (.a(A), .b(B), .out(subtractor_1_out));  // open: bin, bout
  assign or_1_out = A | B;  // OR_Gate or_1, 32 bits wide
  Multiplexer #(.select(3), .width(32), .enable("false")) multiplexer_1 (
    .in0(adder_1_out), .in1(subtractor_1_out), .in2(or_1_out), .out(ALUOut), .sel(ALUCtr));  // open: in3, in4, in5, in6, in7
endmodule

module EXT (
  input  [15:0] Imm,
  input  [1:0] EXTCtr,
  output [31:0] ExtOut
);

  wire [31:0] bit_extender_1_out, bit_extender_2_out;

  assign bit_extender_1_out = {{16{1'b0}}, Imm};  // Bit_Extender bit_extender_1
  assign bit_extender_2_out = {{16{Imm[15]}}, Imm};  // Bit_Extender bit_extender_2
  Multiplexer #(.select(2), .width(32), .enable("false")) multiplexer_1 (
    .in0(bit_extender_1_out), .in1(bit_extender_2_out), .in2({Imm, {16{1'b0}}}), .out(ExtOut), .sel(EXTCtr));  // open: in3
endmodule

module DM (
  input  [4:0] MemAddr,
  input  [31:0] wd,
  input  clk,
  input  rst,
  input  MemWrite,
  output [31:0] data
);

  wire not_1_out;

  RAM #(.addrWidth(5), .dataWidth(32), .bus("separate")) ram_1 (
    .addr(MemAddr), .din(wd), .data(data), .str(MemWrite), .clk(clk), .ld(not_1_out), .clr(rst));  // open: sel
  not not_1 (not_1_out, MemWrite);
endmodule

module IFU (
  input  [1:0] Br,
  input  equal,
  input  less,
  input  greater,
  input  in_5,
  input  rst,
  output [31:0] out_7
);

  wire or_1_out;
  wire [31:0] adder_1_out, adder_2_out, multiplexer_1_out, multiplexer_2_out, multiplexer_3_out, PC_q;
  wire [31:2] bit_extender_1_out;

  Register #(.width(32)) PC (.D(multiplexer_3_out), .Q(PC_q), .clk(in_5), .clr(rst));  // open: en
  Adder #(.width(32)) adder_1 (.a(PC_q), .b(32'h4), .out(adder_1_out));  // open: cin, cout
  or or_1 (or_1_out, equal, less);
  Adder #(.width(32)) adder_2 (.a(adder_1_out), .b({bit_extender_1_out, 2'b00}), .out(adder_2_out));  // open: cin, cout
  assign bit_extender_1_out = {{14{out_7[15]}}, out_7[15:0]};  // Bit_Extender bit_extender_1
  Multiplexer #(.width(32), .enable("false")) multiplexer_1 (
    .in0(adder_1_out), .in1(adder_2_out), .out(multiplexer_1_out), .sel(equal));
  Multiplexer #(.width(32), .enable("false")) multiplexer_2 (
    .in0(adder_1_out), .in1(adder_2_out), .out(multiplexer_2_out), .sel(or_1_out));
  Multiplexer #(.select(2), .width(32), .enable("false")) multiplexer_3 (
    .in0(adder_1_out), .in1(multiplexer_1_out), .in2({out_7[31:28], out_7[25:0], 2'b00}),
    .in3(multiplexer_2_out), .out(multiplexer_3_out), .sel(Br));
  ROM #(.addrWidth(5), .dataWidth(32)) rom_1 (.addr(PC_q[6:2]), .data(out_7));  // open: sel

  // Notes on the sheet:
  //   contents of rom_1 (hex, n*v repeats v):
  //   240c0005 110c0002 25080001 8000001 2402000a 19c0fffb
endmodule

module Controller (
  input  [5:0] op,
  input  [5:0] func,
  output WACtr,
  output [1:0] WDCtr,
  output [1:0] EXTCtr,
  output BCtr,
  output [2:0] ALUCtr,
  output MemWrite,
  output WE,
  output [1:0] BrCtr
);

  wire cand_1_addiu, cand_1_addu, cand_1_beq, cand_1_blez, cand_1_j, cand_1_lui, cand_1_lw, cand_1_ori,
       cand_1_subu, cand_1_sw;

  CAnd cand_1 (
    .op5(op[5]), .op4(op[4]), .op3(op[3]), .op2(op[2]), .op1(op[1]), .op0(op[0]), .f5(func[5]), .f4(func[4]),
    .f3(func[3]), .f2(func[2]), .f1(func[1]), .f0(func[0]), .addu(cand_1_addu), .subu(cand_1_subu),
    .ori(cand_1_ori), .lw(cand_1_lw), .sw(cand_1_sw), .beq(cand_1_beq), .lui(cand_1_lui), .j(cand_1_j),
    .addiu(cand_1_addiu), .blez(cand_1_blez));
  COr cor_1 (
    .addu(cand_1_addu), .subu(cand_1_subu), .ori(cand_1_ori), .lw(cand_1_lw), .sw(cand_1_sw),
    .beq(cand_1_beq), .lui(cand_1_lui), .j(cand_1_j), .addiu(cand_1_addiu), .blez(cand_1_blez),
    .WACtr(WACtr), .WDCtr1(WDCtr[1]), .WDCtr0(WDCtr[0]), .EXTCtr1(EXTCtr[1]), .EXTCtr0(EXTCtr[0]),
    .BCtr(BCtr), .ALUCtr2(ALUCtr[2]), .ALUCtr1(ALUCtr[1]), .ALUCtr0(ALUCtr[0]), .MemWrite(MemWrite), .WE(WE),
    .BrCtr0(BrCtr[0]), .BrCtr1(BrCtr[1]));
endmodule

module CAnd (
  input  op5,
  input  op4,
  input  op3,
  input  op2,
  input  op1,
  input  op0,
  input  f5,
  input  f4,
  input  f3,
  input  f2,
  input  f1,
  input  f0,
  output addu,
  output subu,
  output ori,
  output lw,
  output sw,
  output beq,
  output lui,
  output j,
  output addiu,
  output blez
);

  wire not_1_out, not_2_out, not_3_out, not_4_out, not_5_out, not_6_out, not_7_out, not_8_out, not_9_out,
       not_10_out, not_11_out, not_12_out, not_13_out, not_14_out, not_15_out, not_16_out, not_17_out,
       not_18_out, not_19_out, not_20_out, not_21_out, not_22_out, not_23_out, not_24_out, not_25_out,
       not_26_out, not_27_out, not_28_out, not_29_out, not_30_out, not_31_out, not_32_out, not_33_out,
       not_34_out, not_35_out, not_36_out, not_37_out, not_38_out, not_39_out, not_40_out, not_41_out,
       not_42_out, not_43_out, not_44_out, not_45_out, not_46_out, not_47_out;

  not not_1 (not_1_out, op5);
  not not_2 (not_2_out, op4);
  not not_3 (not_3_out, op3);
  not not_4 (not_4_out, op2);
  not not_5 (not_5_out, op1);
  not not_6 (not_6_out, op0);
  not not_7 (not_7_out, f4);
  not not_8 (not_8_out, f3);
  not not_9 (not_9_out, f2);
  not not_10 (not_10_out, f1);
  not not_11 (not_11_out, op5);
  not not_12 (not_12_out, op4);
  not not_13 (not_13_out, op3);
  not not_14 (not_14_out, op2);
  not not_15 (not_15_out, op1);
  not not_16 (not_16_out, op0);
  not not_17 (not_17_out, f4);
  not not_18 (not_18_out, f3);
  not not_19 (not_19_out, f2);
  not not_20 (not_20_out, op5);
  not not_21 (not_21_out, op4);
  not not_22 (not_22_out, op1);
  not not_23 (not_23_out, op4);
  not not_24 (not_24_out, op3);
  not not_25 (not_25_out, op2);
  not not_26 (not_26_out, op4);
  not not_27 (not_27_out, op2);
  not not_28 (not_28_out, op5);
  not not_29 (not_29_out, op4);
  not not_30 (not_30_out, op3);
  not not_31 (not_31_out, op1);
  not not_32 (not_32_out, op0);
  not not_33 (not_33_out, op5);
  not not_34 (not_34_out, op4);
  not not_35 (not_35_out, op5);
  not not_36 (not_36_out, op4);
  not not_37 (not_37_out, op3);
  not not_38 (not_38_out, op2);
  not not_39 (not_39_out, op0);
  not not_40 (not_40_out, op5);
  not not_41 (not_41_out, op4);
  not not_42 (not_42_out, op2);
  not not_43 (not_43_out, op1);
  not not_44 (not_44_out, op5);
  not not_45 (not_45_out, op4);
  not not_46 (not_46_out, op3);
  not not_47 (not_47_out, op0);
  and and_1 (ori, not_20_out, not_21_out, op3, op2, not_22_out, op0);
  and and_2 (lw, op5, not_23_out, not_24_out, not_25_out, op1, op0);
  and and_3 (sw, op5, not_26_out, op3, not_27_out, op1, op0);
  and and_4 (beq, not_28_out, not_29_out, not_30_out, op2, not_31_out, not_32_out);
  and and_5 (lui, not_33_out, not_34_out, op3, op2, op1, op0);
  and and_6 (j, not_35_out, not_36_out, not_37_out, not_38_out, op1, not_39_out);
  and and_7 (addiu, not_40_out, not_41_out, op3, not_42_out, not_43_out, op0);
  and and_8 (blez, not_44_out, not_45_out, not_46_out, op2, op1, not_47_out);
  and and_9 (addu, not_1_out, not_2_out, not_3_out, not_4_out, not_5_out, not_6_out, f5, not_7_out, not_8_out, not_9_out, not_10_out, f0);
  and and_10 (subu, not_11_out, not_12_out, not_13_out, not_14_out, not_15_out, not_16_out, f5, not_17_out, not_18_out, not_19_out, f1, f0);
endmodule

module COr (
  input  addu,
  input  subu,
  input  ori,
  input  lw,
  input  sw,
  input  beq,
  input  lui,
  input  j,
  input  addiu,
  input  blez,
  output WACtr,
  output WDCtr1,
  output WDCtr0,
  output EXTCtr1,
  output EXTCtr0,
  output BCtr,
  output ALUCtr2,
  output ALUCtr1,
  output ALUCtr0,
  output MemWrite,
  output WE,
  output BrCtr0,
  output BrCtr1
);

  or or_1 (WACtr, lw, ori, lui, addiu);
  or or_2 (EXTCtr1, beq, lui);
  or or_3 (EXTCtr0, lw, sw, addiu);
  or or_4 (BCtr, ori, lw, sw, addiu);
  or or_5 (WE, ori, addu, subu, lw, lui, addiu);
  or or_6 (BrCtr0, beq, blez);
  or or_7 (BrCtr1, j, blez);

  assign ALUCtr0 = subu;
  assign ALUCtr1 = ori;
  assign ALUCtr2 = 1'b0;
  assign MemWrite = sw;
  assign WDCtr0 = lw;
  assign WDCtr1 = lui;
endmodule

module RF (
  input  in_1,
  input  [4:0] RA1,
  input  [4:0] RA2,
  input  [4:0] WA,
  input  [31:0] WD,
  input  clk,
  input  rst,
  output [31:0] out_8,
  output [31:0] out_9
);

  wire WE00, WE01, WE02, WE03, WE04, WE05, WE06, WE07, WE08, WE09, WE10, WE11, WE12, WE13, WE14, WE15, WE16,
       WE17, WE18, WE19, WE20, WE21, WE22, WE23, WE24, WE25, WE26, WE27, WE28, WE29, WE30, WE31;
  wire [31:0] Out00, Out01, Out02, Out03, Out04, Out05, Out06, Out07, Out08, Out09, Out10, Out11, Out12,
       Out13, Out14, Out15, Out16, Out17, Out18, Out19, Out20, Out21, Out22, Out23, Out24, Out25, Out26,
       Out27, Out28, Out29, Out30, Out31;

  Demultiplexer #(.select(5), .enable("false")) demultiplexer_1 (
    .out0(WE00), .out1(WE01), .out2(WE02), .out3(WE03), .out4(WE04), .out5(WE05), .out6(WE06), .out7(WE07),
    .out8(WE08), .out9(WE09), .out10(WE10), .out11(WE11), .out12(WE12), .out13(WE13), .out14(WE14),
    .out15(WE15), .out16(WE16), .out17(WE17), .out18(WE18), .out19(WE19), .out20(WE20), .out21(WE21),
    .out22(WE22), .out23(WE23), .out24(WE24), .out25(WE25), .out26(WE26), .out27(WE27), .out28(WE28),
    .out29(WE29), .out30(WE30), .out31(WE31), .in(in_1), .sel(WA));
  Register #(.width(32)) register_1 (.D({32{1'b0}}), .en(WE00), .Q(Out00), .clk(clk), .clr(rst));
  Register #(.width(32)) register_2 (.D(WD), .en(WE08), .Q(Out08), .clk(clk), .clr(rst));
  Register #(.width(32)) register_3 (.D(WD), .en(WE16), .Q(Out16), .clk(clk), .clr(rst));
  Register #(.width(32)) register_4 (.D(WD), .en(WE24), .Q(Out24), .clk(clk), .clr(rst));
  Register #(.width(32)) register_5 (.D(WD), .en(WE01), .Q(Out01), .clk(clk), .clr(rst));
  Register #(.width(32)) register_6 (.D(WD), .en(WE09), .Q(Out09), .clk(clk), .clr(rst));
  Register #(.width(32)) register_7 (.D(WD), .en(WE17), .Q(Out17), .clk(clk), .clr(rst));
  Register #(.width(32)) register_8 (.D(WD), .en(WE25), .Q(Out25), .clk(clk), .clr(rst));
  Register #(.width(32)) register_9 (.D(WD), .en(WE02), .Q(Out02), .clk(clk), .clr(rst));
  Register #(.width(32)) register_10 (.D(WD), .en(WE10), .Q(Out10), .clk(clk), .clr(rst));
  Register #(.width(32)) register_11 (.D(WD), .en(WE18), .Q(Out18), .clk(clk), .clr(rst));
  Register #(.width(32)) register_12 (.D(WD), .en(WE26), .Q(Out26), .clk(clk), .clr(rst));
  Register #(.width(32)) register_13 (.D(WD), .en(WE03), .Q(Out03), .clk(clk), .clr(rst));
  Register #(.width(32)) register_14 (.D(WD), .en(WE11), .Q(Out11), .clk(clk), .clr(rst));
  Register #(.width(32)) register_15 (.D(WD), .en(WE19), .Q(Out19), .clk(clk), .clr(rst));
  Register #(.width(32)) register_16 (.D(WD), .en(WE27), .Q(Out27), .clk(clk), .clr(rst));
  Multiplexer #(.select(5), .width(32), .enable("false")) multiplexer_1 (
    .in0(Out00), .in1(Out01), .in2(Out02), .in3(Out03), .in4(Out04), .in5(Out05), .in6(Out06), .in7(Out07),
    .in8(Out08), .in9(Out09), .in10(Out10), .in11(Out11), .in12(Out12), .in13(Out13), .in14(Out14),
    .in15(Out15), .in16(Out16), .in17(Out17), .in18(Out18), .in19(Out19), .in20(Out20), .in21(Out21),
    .in22(Out22), .in23(Out23), .in24(Out24), .in25(Out25), .in26(Out26), .in27(Out27), .in28(Out28),
    .in29(Out29), .in30(Out30), .in31(Out31), .out(out_8), .sel(RA1));
  Multiplexer #(.select(5), .width(32), .enable("false")) multiplexer_2 (
    .in0(Out00), .in1(Out01), .in2(Out02), .in3(Out03), .in4(Out04), .in5(Out05), .in6(Out06), .in7(Out07),
    .in8(Out08), .in9(Out09), .in10(Out10), .in11(Out11), .in12(Out12), .in13(Out13), .in14(Out14),
    .in15(Out15), .in16(Out16), .in17(Out17), .in18(Out18), .in19(Out19), .in20(Out20), .in21(Out21),
    .in22(Out22), .in23(Out23), .in24(Out24), .in25(Out25), .in26(Out26), .in27(Out27), .in28(Out28),
    .in29(Out29), .in30(Out30), .in31(Out31), .out(out_9), .sel(RA2));
  Register #(.width(32)) register_17 (.D(WD), .en(WE04), .Q(Out04), .clk(clk), .clr(rst));
  Register #(.width(32)) register_18 (.D(WD), .en(WE12), .Q(Out12), .clk(clk), .clr(rst));
  Register #(.width(32)) register_19 (.D(WD), .en(WE20), .Q(Out20), .clk(clk), .clr(rst));
  Register #(.width(32)) register_20 (.D(WD), .en(WE28), .Q(Out28), .clk(clk), .clr(rst));
  Register #(.width(32)) register_21 (.D(WD), .en(WE05), .Q(Out05), .clk(clk), .clr(rst));
  Register #(.width(32)) register_22 (.D(WD), .en(WE13), .Q(Out13), .clk(clk), .clr(rst));
  Register #(.width(32)) register_23 (.D(WD), .en(WE21), .Q(Out21), .clk(clk), .clr(rst));
  Register #(.width(32)) register_24 (.D(WD), .en(WE29), .Q(Out29), .clk(clk), .clr(rst));
  Register #(.width(32)) register_25 (.D(WD), .en(WE06), .Q(Out06), .clk(clk), .clr(rst));
  Register #(.width(32)) register_26 (.D(WD), .en(WE14), .Q(Out14), .clk(clk), .clr(rst));
  Register #(.width(32)) register_27 (.D(WD), .en(WE22), .Q(Out22), .clk(clk), .clr(rst));
  Register #(.width(32)) register_28 (.D(WD), .en(WE30), .Q(Out30), .clk(clk), .clr(rst));
  Register #(.width(32)) register_29 (.D(WD), .en(WE07), .Q(Out07), .clk(clk), .clr(rst));
  Register #(.width(32)) register_30 (.D(WD), .en(WE15), .Q(Out15), .clk(clk), .clr(rst));
  Register #(.width(32)) register_31 (.D(WD), .en(WE23), .Q(Out23), .clk(clk), .clr(rst));
  Register #(.width(32)) register_32 (.D(WD), .en(WE31), .Q(Out31), .clk(clk), .clr(rst));

  // Other names for the same wires on the sheet: RD1[31:0] = out_8; RD2[31:0] = out_9
endmodule

module Decoder (
  input  [31:0] in_1,
  output [5:0] op,
  output [4:0] rs,
  output [4:0] rt,
  output [4:0] rd,
  output [4:0] shamt,
  output [5:0] func,
  output [15:0] Imm
);


  assign func = in_1[5:0];
  assign Imm = in_1[15:0];
  assign op = in_1[31:26];
  assign rd = in_1[15:11];
  assign rs = in_1[25:21];
  assign rt = in_1[20:16];
  assign shamt = in_1[10:6];
endmodule
